# Fritzing sketch owl_lite_unit (saved by Fritzing 0.7.12b)
breadboards: 1

parts:
  Part1 = Arduino Pro Mini 3.3V
  VCC1 = Battery
  Part2 = Adafruit RFM69HCW Transceiver Radio [part_number="Adafruit #3070 and #3071"]
  S3 = Toggle Switch [package=THT]
  S4 = Toggle Switch [package=THT]
  Q2 = NPN-Transistor [package="SOT-23 [SMD]"]
  J2 = Piezo Speaker
  S5 = Pushbutton [package="[THT]"]
  R1 = 220 Ω Resistor [package=THT]
  S6 = Pushbutton [package=THT]

nets:
  N1: Part1.MOSI, Part2.MOSI
  N2: Part1.D10, Part2.CS
  N3: Part1.D9, Part2.RST
  N4: Part1.D2, Part2.DIO0
  N5: VCC1.-, Part2.GND, S4.L2, J2.pin1, S6.Pin_1, S6.Pin_2
  N6: VCC1.+, Part2.VIN, S4.L1, Q2.2
  N7: Part2.ANTENNA, S3.COM
  N8: Q2.0, S5.Pin_1, S5.Pin_2
  N9: Q2.1, J2.pin2
  N10: S5.Pin_3, S5.Pin_4, R1.Pin_1
  N11: S6.Pin_3, S6.Pin_4

notes:
  to external charger (USB or barrel jack)
  1/4 wave antenna
  to SMA adapter for external antenna
  Leave this part open for optional FTDI connector
  currently all Owls are powered by smaller Li-ion batteries, although AA or AAA could also work
  For manufactured Owls, these buttons are both external momentary push buttons. Pin 7 should be set up with pullup resistor in software in order to function properly

custom parts:
  Adafruit RFM69HCW Transceiver Radio: Sending data over long distances is like magic, and now you can be a magician with this range of powerful and easy-to-use radio modules. Sure, sometimes you want to talk to a computer (a good time to use WiFi) or perhaps communicate with a Phone (choose Bluetooth Low Energy!) but what if you want to send data very far? Most WiFi, Bluetooth, Zigbee and other wireless chipsets use 2.4GHz, which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
  Pushbutton: Start and stop timer
