# Fritzing sketch owl_unit (saved by Fritzing 0.7.12b)
breadboards: 1

parts:
  Part1 = Adafruit Feather M0 RFM9x LoRa [part_number="Adafruit #3178 or #3179"]
  J1 = Piezo Speaker
  Q1 = NPN-Transistor [package="SOT-23 [SMD]"]
  S1 = Toggle Switch [package=THT]
  S2 = Toggle Switch [package=THT]
  LED5 = yellow smd LED [package="0805 [SMD]"]  # not connected
  R2 = 220 Ω Resistor [package=THT]
  S6 = Pushbutton [package="[THT]"]
  S7 = Pushbutton [package="[THT]"]

nets:
  N1: Part1.ANT, S1.COM
  N2: Part1.GND, Part1.D6, J1.pin1, S2.L1, S6.Pin_1, S6.Pin_2, S6.Pin_3, S6.Pin_4, S7.Pin_3, S7.Pin_4
  N3: Part1.VBAT, Q1.2, S2.L2
  N4: Part1.D12, S2.COM
  N5: J1.pin2, Q1.1
  N6: Q1.0, R2.Pin_1
  N7: S7.Pin_1, S7.Pin_2

notes:
  78 mm 1/4 wave antenna
  to SMA adapter for external antenna
  add header pins or maybe external ports to add sensors
  External Switch for mode selection
  For manufactured Owls, these buttons are both external momentary push buttons. Pin 6 should be set up with pullup resistor in software in order to function properly

custom parts:
  Adafruit Feather M0 RFM9x LoRa: This is the Adafruit Feather M0 RFM95 LoRa Radio - our take on an microcontroller with a "Long Range (LoRa)" packet radio transceiver with built in USB and battery charging. Its an Adafruit Feather M0 with a 433Mhz or 900MHz radio module cooked in! Great for making wireless networks that are more flexible than Bluetooth LE and without the high power requirements of WiFi. We have other boards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
  Pushbutton: Start and stop timer
