# Fritzing sketch owl_unit_LEDs (saved by Fritzing 0.7.12b)
breadboards: 1

parts:
  Part1 = Adafruit Feather M0 RFM9x LoRa [part_number="Adafruit #3178 or #3179"]
  J1 = Piezo Speaker
  Q1 = NPN-Transistor [package="SOT-23 [SMD]"]
  LED1 = LED - 3mm [color="Red (633nm)" package="3 mm [THT]"]
  LED2 = yellow smd LED [package="0805 [SMD]"]
  LED3 = yellow smd LED [package="0805 [SMD]"]
  LED4 = yellow smd LED [package="0805 [SMD]"]
  S1 = Toggle Switch [package=THT]
  S2 = Toggle Switch [package=THT]
  LED5 = yellow smd LED [package="0805 [SMD]"]  # not connected
  R2 = 220 Ω Resistor [package=THT]
  S6 = Pushbutton [package="[THT]"]

nets:
  N1: Part1.ANT, S1.COM
  N2: Part1.GND, J1.pin1, LED1.cathode, LED2.cathode, LED3.cathode, LED4.cathode, S2.L1, S6.Pin_1, S6.Pin_2, S6.Pin_3, S6.Pin_4
  N3: Part1.VBAT, Q1.1, S2.L2
  N4: Part1.D12, S2.COM
  N5: Part1.D11, LED4.anode
  N6: Part1.D10, LED3.anode
  N7: Part1.D9, LED2.anode
  N8: Part1.D6, LED1.anode
  N9: Part1.D5, R2.Pin_1
  N10: J1.pin2, Q1.2
  N11: Q1.0, R2.Pin_0

notes:
  78 mm 1/4 wave antenna
  to SMA adapter for external antenna
  External Switch for mode selection
  Speaker activation button

custom parts:
  Adafruit Feather M0 RFM9x LoRa: This is the Adafruit Feather M0 RFM95 LoRa Radio - our take on an microcontroller with a "Long Range (LoRa)" packet radio transceiver with built in USB and battery charging. Its an Adafruit Feather M0 with a 433Mhz or 900MHz radio module cooked in! Great for making wireless networks that are more flexible than Bluetooth LE and without the high power requirements of WiFi. We have other boards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
  Pushbutton: Start and stop timer
