# Fritzing sketch owl_lite_unit (saved by Fritzing 0.7.12b)
breadboards: 1

parts:
  Part1 = Arduino Pro Mini 3.3V
  VCC1 = Battery
  Part2 = Adafruit RFM69HCW Transceiver Radio [part_number="Adafruit #3070 and #3071"]
  S3 = Toggle Switch [package=THT]
  LED5 = yellow smd LED [package="0805 [SMD]"]
  LED6 = yellow smd LED [package="0805 [SMD]"]
  LED8 = yellow smd LED [package="0805 [SMD]"]
  LED7 = Red smd LED [package="0805 [SMD]"]
  S4 = Toggle Switch [package=THT]
  Q2 = NPN-Transistor [package="SOT-23 [SMD]"]
  J2 = Piezo Speaker
  S5 = Pushbutton [package="[THT]"]
  R1 = 33k Ω Resistor [package=THT]
  R2 = Resistor [tolerance=±5% resistance=10k package=THT]

nets:
  N1: Part1.MOSI, Part2.MOSI
  N2: Part1.D10, Part2.CS
  N3: Part1.D9, Part2.RST
  N4: Part1.D2, Part2.DIO0
  N5: VCC1.-, Part2.GND, LED5.cathode, LED6.cathode, LED8.cathode, LED7.cathode, S4.L2, J2.pin1, R2.Pin_1
  N6: VCC1.+, Part2.VIN, S4.L1, Q2.2, R1.Pin_0
  N7: Part2.ANTENNA, S3.COM
  N8: Q2.0, S5.Pin_1, S5.Pin_2
  N9: Q2.1, J2.pin2
  N10: S5.Pin_3, S5.Pin_4
  N11: R1.Pin_1, R2.Pin_0

notes:
  to external charger (USB or barrel jack)
  1/4 wave antenna
  to SMA adapter for external antenna
  Leave this part open for optional FTDI connector
  optional voltage divider for reading battery power

custom parts:
  Adafruit RFM69HCW Transceiver Radio: Sending data over long distances is like magic, and now you can be a magician with this range of powerful and easy-to-use radio modules. Sure, sometimes you want to talk to a computer (a good time to use WiFi) or perhaps communicate with a Phone (choose Bluetooth Low Energy!) but what if you want to send data very far? Most WiFi, Bluetooth, Zigbee and other wireless chipsets use 2.4GHz, which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
  Pushbutton: Start and stop timer
